# Fritzing sketch tank sensor (saved by Fritzing 0.9.3b)
breadboards: 1

parts:
  Part1 = Arduino Nano (Rev3.0)
  U1 = RELAY [package=relay-t9a]
  U2 = Voltage Regulator - 5V [package="TO220 [THT]"]
  U3 = LIPO-1000mAh [package=lipo-1000]
  U4 = LIPO-1000mAh [package=lipo-1000]  # not connected
  U5 = LIPO-1000mAh [package=lipo-1000]
  M1 = DC Motor

nets (from the schematic view):
  N1: Part1.D2, U1.COIL1
  N2: Part1.VIN, U2.output_voltage
  N3: U1.COIL2, U2.GND, U5.-, M1.pin_2
  N4: U1.MAIN, U2.input_voltage, U3.+
  N5: U1.NC, M1.pin_1
